# Fritzing sketch arduino (saved by Fritzing 1.0.3b)
breadboards: 1

parts:
  R1 = Resistor [tolerance=±5% power=0.25W resistance=220 package=THT]
  DME_Station_Relaiskontakt = TILT-SWITCH-SW-200D [package=reed_switch_plastic]
  R2 = Resistor [tolerance=±5% power=0.25W resistance=220 package=THT]
  Mod1 = Amica NodeMCU DEVKIT 1.0
  LED_Strip_1 = WS2812 RGB LED strip
  Bauteil1 = Arduino Uno (Rev3)

nets:
  GND: R1.Pin_0, LED_Strip_1.GND, Bauteil1.GND
  N1: R1.Pin_1, DME_Station_Relaiskontakt.2, Bauteil1.D7
  VCC: DME_Station_Relaiskontakt.1, LED_Strip_1.VCC, Bauteil1.5V
  N2: R2.Pin_0, Bauteil1.D8
  N3: R2.Pin_1, LED_Strip_1.DIN
  N4: Mod1.pin_12, Bauteil1.D0/RX
  N5: Mod1.pin_13, Bauteil1.D1/TX

custom parts:
  WS2812 RGB LED strip: WS2812 strip
