# Fritzing sketch schaltung1 (saved by Fritzing 1.0.3b)
breadboards: 1

parts:
  DME_Station_Relaiskontakt = SWITCH-MOMENTARY-2 [package=tactile-switch-1101ne]
  Bauteil1 = Arduino Uno (Rev3)

nets:
  N1: DME_Station_Relaiskontakt.1, Bauteil1.3V3
  N2: DME_Station_Relaiskontakt.2, Bauteil1.A0
